# Fritzing sketch ArdunioConversion (saved by Fritzing 0.9.4)

parts:
  A1 = Teensy 4.0
  J2 = female pin header, 17 pins [form="♀ (female)"]
  J3 = female pin header, 17 pins [form="♀ (female)"]
  J4 = Basic Force Sensing Resistor (FSR) [package=THT]
  R1 = Resistor [tolerance=±5% resistance=100k package="0603 [SMD]"]

nets:
  N1: A1.pin_1, J2.pin1, R1.Pin_0
  N2: A1.pin_5, J2.pin6
  N3: A1.pin_6, J2.pin7
  N4: A1.pin_8, J2.pin9
  N5: A1.pin_9, J2.pin10
  N6: A1.pin_13, J2.pin16
  N7: A1.pin_14, J2.pin17
  N8: A1.pin_26, J4.pin_1
  N9: A1.pin_27, J3.pin10
  N10: A1.pin_28, J3.pin9
  N11: A1.pin_29, J3.pin8
  N12: A1.pin_30, J3.pin7
  N13: A1.pin33, J2.pin2, J4.pin_0

notes:
  rightDirectionB = A2; //"counterclockwise" input
  rightDirectionA = A3; //"clockwise" input
  leftDirectionB = A4; //"counterclockwise" input
  leftDirectionA = A5; //"clockwise" input
  OLD
  PWM rightSpeedPin = 11
  PWM leftSpeedPin = 10
  rightEncoderB = 8
  rightEncoderA = 7
  leftEncoderB = 1
  leftEncoderA = 0
  OLD
  PWM rightSpeedPin = 3
  PWM leftSpeedPin = 4
  rightEncoderB = 6
  rightEncoderA = 7
  leftEncoderB = 11
  leftEncoderA = 12
  New
  rightDirectionB = A9; //"counterclockwise" input
  rightDirectionA = A8; //"clockwise" input
  leftDirectionB = A7; //"counterclockwise" input
  leftDirectionA = A6; //"clockwise" input
  New

custom parts:
  Teensy 4.0: The Teensy is a complete USB-based microcontoller development system, in a very small footprint, capable of implementing many types of projects. All programming is done via the USB port. No special programmer is needed, only a standard micro-USB cable and a PC or Macintosh with a USB port. (Oct 2023 added the VBUS pad at user request.)
